# Fritzing sketch Schema (saved by Fritzing 0.9.3b)
breadboards: 1

parts:
  Componente1 = Arduino Mega 2560 (Rev3)
  S1 = Pushbutton [package="[THT]"]
  S2 = Pushbutton [package="[THT]"]
  S3 = Pushbutton [package="[THT]"]
  R1 = Resistor [tolerance=±5% resistance=220 package=THT]
  R2 = Resistor [tolerance=±5% resistance=220 package="2010 [SMD]"]
  R3 = Resistor [tolerance=±5% resistance=220 package="2010 [SMD]"]
  7_Segment1 = 7 Segment Display
  7_Segment2 = 7 Segment Display
  LED1 = 7-SEGMENT-4DIGIT-YOUNGSUN [package=7-segment-4digit-youngsun]  # not connected
  R4 = Resistor [tolerance=±5% resistance=220 package="2010 [SMD]"]  # not connected
  R5 = Resistor [tolerance=±5% resistance=220 package="2010 [SMD]"]  # not connected

nets:
  N1: Componente1.5V, Componente1.D2_PWM, Componente1.D3_PWM, Componente1.D5_PWM, S1.Pin_1, S1.Pin_2, S1.Pin_3, S1.Pin_4, S2.Pin_1, S2.Pin_2, S2.Pin_3, S2.Pin_4, S3.Pin_1, S3.Pin_2, S3.Pin_3, S3.Pin_4, R1.Pin_1, R2.Pin_1, R3.Pin_1
  N2: 7_Segment1.Segment_G, 7_Segment1.Segment_F
  N3: 7_Segment1.Segment_B, 7_Segment1.Segment_A
  N4: 7_Segment2.Segment_G, 7_Segment2.Segment_F
  N5: 7_Segment2.Segment_B, 7_Segment2.Segment_A
